# Fritzing sketch wiring (saved by Fritzing 0.9.7b)
breadboards: 3

parts:
  부품1 = Arduino Mega ADK (Rev3)  # not connected
  부품2 = Arduino Mega ADK (Rev3)
  부품3 = Arduino Mega ADK (Rev3)
  A1 = DHT22 module  # not connected
  R3 = Resistor [tolerance=±5% power=0.25 resistance=10k package=THT]
  BIGTREETECH_TMC2209_V1_1 = TMC2209
  BIGTREETECH_TMC2209_V1_2 = TMC2209
  BIGTREETECH_TMC2209_V1_3 = TMC2209
  BIGTREETECH_TMC2209_V1_4 = TMC2209
  BIGTREETECH_TMC2209_V1_5 = TMC2209
  BIGTREETECH_TMC2209_V1_6 = TMC2209
  M1 = Stepper Motor - Bipolar
  M2 = Stepper Motor - Bipolar
  M5 = Stepper Motor - Bipolar
  M6 = Stepper Motor - Bipolar
  M7 = Stepper Motor - Bipolar
  M8 = Stepper Motor - Bipolar

nets:
  N1: 부품2.D13_PWM, BIGTREETECH_TMC2209_V1_1.DIRECTION
  N2: 부품2.D12_PWM, BIGTREETECH_TMC2209_V1_1.STEP
  N3: 부품2.D11_PWM, BIGTREETECH_TMC2209_V1_1.ENABLE
  N4: 부품2.D10_PWM, BIGTREETECH_TMC2209_V1_3.DIRECTION
  N5: 부품2.D9_PWM, BIGTREETECH_TMC2209_V1_3.STEP
  N6: 부품2.D8_PWM, BIGTREETECH_TMC2209_V1_3.ENABLE
  N7: 부품2.D5_PWM, BIGTREETECH_TMC2209_V1_2.ENABLE
  N8: 부품2.D6_PWM, BIGTREETECH_TMC2209_V1_2.STEP
  N9: 부품2.D7_PWM, BIGTREETECH_TMC2209_V1_2.DIRECTION
  N10: 부품3.A0, R3.Pin_1
  N11: 부품3.5V, R3.Pin_0
  N12: BIGTREETECH_TMC2209_V1_1.GROUND_MT, BIGTREETECH_TMC2209_V1_6.GROUND_MT
  N13: BIGTREETECH_TMC2209_V1_1.OUT_B2, M5.D
  N14: BIGTREETECH_TMC2209_V1_1.OUT_A2, M5.A
  N15: BIGTREETECH_TMC2209_V1_1.OUT_A1, M5.C
  N16: BIGTREETECH_TMC2209_V1_1.OUT_B1, M5.B
  VDD: BIGTREETECH_TMC2209_V1_1.VDD, BIGTREETECH_TMC2209_V1_6.VDD
  N17: BIGTREETECH_TMC2209_V1_1.GROUND_LOG, BIGTREETECH_TMC2209_V1_6.GROUND_LOG
  N18: BIGTREETECH_TMC2209_V1_2.OUT_B2, M1.D
  N19: BIGTREETECH_TMC2209_V1_2.OUT_A2, M1.A
  N20: BIGTREETECH_TMC2209_V1_2.OUT_A1, M1.C
  N21: BIGTREETECH_TMC2209_V1_2.OUT_B1, M1.B
  N22: BIGTREETECH_TMC2209_V1_3.OUT_B2, M6.D
  N23: BIGTREETECH_TMC2209_V1_3.OUT_A2, M6.A
  N24: BIGTREETECH_TMC2209_V1_3.OUT_A1, M6.C
  N25: BIGTREETECH_TMC2209_V1_3.OUT_B1, M6.B
  N26: BIGTREETECH_TMC2209_V1_4.OUT_B2, M8.D
  N27: BIGTREETECH_TMC2209_V1_4.OUT_A2, M8.A
  N28: BIGTREETECH_TMC2209_V1_4.OUT_A1, M8.C
  N29: BIGTREETECH_TMC2209_V1_4.OUT_B1, M8.B
  N30: BIGTREETECH_TMC2209_V1_5.ENABLE, BIGTREETECH_TMC2209_V1_6.ENABLE
  N31: BIGTREETECH_TMC2209_V1_5.STEP, BIGTREETECH_TMC2209_V1_6.STEP
  N32: BIGTREETECH_TMC2209_V1_5.DIRECTION, BIGTREETECH_TMC2209_V1_6.DIRECTION
  N33: BIGTREETECH_TMC2209_V1_5.OUT_B2, M7.D
  N34: BIGTREETECH_TMC2209_V1_5.OUT_A2, M7.A
  N35: BIGTREETECH_TMC2209_V1_5.OUT_A1, M7.C
  N36: BIGTREETECH_TMC2209_V1_5.OUT_B1, M7.B
  N37: BIGTREETECH_TMC2209_V1_6.OUT_B2, M2.D
  N38: BIGTREETECH_TMC2209_V1_6.OUT_A2, M2.A
  N39: BIGTREETECH_TMC2209_V1_6.OUT_A1, M2.C
  N40: BIGTREETECH_TMC2209_V1_6.OUT_B1, M2.B

notes:
  DDDOT
  CNSWW
  24V

custom parts:
  DHT22 module: DHT22 module. Pins VCC Data GND.
  TMC2209: This is a Stepper Motor Controller for integrated circuits.
